# Fritzing sketch Untitled Sketch 2 (saved by Fritzing 0.9.3b)
breadboards: 1

parts:
  Part1 = Arduino Uno (Rev3) - ICSP
  Chirp!_Soil_Moisture_Sensor1 = Chirp! Soil Moisture Sensor v2.7.3
  M1 = DC Motor
  WeMos_D1_Mini_Relay_Shield1 = WeMos D1 Mini Relay Shield
  Part2 = Barometric Pressure Sensor - BMP180 Breakout (GY-68)

nets:
  N1: Part1.A0, Chirp!_Soil_Moisture_Sensor1.Pin_0
  N2: Part1.A4/SDA, Part2.SCL
  N3: Part1.A5/SCL, Part2.SDA
  N4: Part1.D2, WeMos_D1_Mini_Relay_Shield1.D4
  5V: Part1.5V, Chirp!_Soil_Moisture_Sensor1.Pin_1, Part2.VCC
  GND: Part1.GND, Chirp!_Soil_Moisture_Sensor1.pin_5, WeMos_D1_Mini_Relay_Shield1.G, Part2.GND
  VIN: Part1.VIN, WeMos_D1_Mini_Relay_Shield1.5V
  N5: M1.pin_1, WeMos_D1_Mini_Relay_Shield1.D8
  N6: M1.pin_2, WeMos_D1_Mini_Relay_Shield1.3V3
